// Logisim project wk6ex1-4.circ as structural Verilog: 12 circuits, main circuit MyXOR
module MyXOR (
  input  X,
  input  Y,
  output out_3
);

  wire and_1_out, and_2_out, not_1_out, not_2_out;

  not not_1 (not_1_out, X);
  not not_2 (not_2_out, Y);
  and and_1 (and_1_out, not_1_out, Y);
  and and_2 (and_2_out, not_2_out, X);
  or or_1 (out_3, and_1_out, and_2_out);

  // Notes on the sheet:
  //   Hier kan je een XOR-schakeling bouwen
  //   Je kan de tutorial volgen (in het Help-menu; "tutorial") of zelf de oplossing bedenken...
endmodule

module FullAdder (
  input  X,
  input  Y,
  input  CarryIn,
  output Sum,
  output CarryOut
);

  wire and_1_out, and_2_out, and_3_out, and_4_out, and_5_out, and_6_out, and_7_out, and_8_out, not_1_out,
       not_2_out, not_3_out;

  not not_1 (not_1_out, X);
  not not_2 (not_2_out, Y);
  not not_3 (not_3_out, CarryIn);
  and and_1 (and_1_out, not_1_out, not_2_out, CarryIn);
  and and_2 (and_2_out, not_3_out, not_3_out, Y, not_1_out);
  and and_3 (and_3_out, X, not_2_out, not_3_out);
  and and_4 (and_4_out, X, Y, CarryIn);
  and and_5 (and_5_out, X, Y, CarryIn);
  and and_6 (and_6_out, X, Y, not_3_out);
  and and_7 (and_7_out, X, not_2_out, CarryIn);
  and and_8 (and_8_out, not_1_out, Y, CarryIn);
  or or_1 (Sum, and_1_out, and_2_out, and_3_out, and_4_out);
  or or_2 (CarryOut, and_5_out, and_6_out, and_7_out, and_8_out);

  // Notes on the sheet:
  //   3 invoerbits:  X,  Y en CarryIn
  //   Hier kan je een FULL-ADDERschakeling bouwen
  //   (1) teken de andere vier rails   (2) je hebt 8 AND-poorten nodig    (3)  je hebt twee OR-poorten nodig
  //   twee uitvoerbits:  Sum en CarryOut
  //   Carry bij: 2 of 3 1tjes
endmodule

module Een_4bit_Ripple_Carry_Adder (
  input  Y3,
  input  Y2,
  input  Y1,
  input  Y0,
  input  X3,
  input  X2,
  input  X1,
  input  X0,
  output Sum4,
  output Sum3,
  output Sum2,
  output Sum1,
  output Sum0
);

  wire fulladder_2_carryout, fulladder_3_carryout, fulladder_4_carryout;

  FullAdder fulladder_1 (.X(X3), .Y(Y3), .CarryIn(fulladder_2_carryout), .Sum(Sum3), .CarryOut(Sum4));
  FullAdder fulladder_2 (.X(X2), .Y(Y2), .CarryIn(fulladder_3_carryout), .Sum(Sum2), .CarryOut(fulladder_2_carryout));
  FullAdder fulladder_3 (.X(X1), .Y(Y1), .CarryIn(fulladder_4_carryout), .Sum(Sum1), .CarryOut(fulladder_3_carryout));
  FullAdder fulladder_4 (.X(X0), .Y(Y0), .CarryIn(1'b0), .Sum(Sum0), .CarryOut(fulladder_4_carryout));

  // Notes on the sheet:
  //   Hier kan je een 4-bit-RIPPLE-CARRY-ADDERschakeling bouwen
  //   8 invoerbits
  //   5 uitvoerbits
endmodule

module Een_4bit_vermenigvuldiger (
  input  Y3,
  input  Y2,
  input  Y1,
  input  Y0,
  input  X3,
  input  X2,
  input  X1,
  input  X0,
  output Z7,
  output Z6,
  output Z5,
  output Z4,
  output Z3,
  output Z2,
  output Z1,
  output Z0
);

  wire een_4bit_ripple_carry_adder_1_sum1, een_4bit_ripple_carry_adder_1_sum2,
       een_4bit_ripple_carry_adder_1_sum3, een_4bit_ripple_carry_adder_1_sum4,
       een_4bit_ripple_carry_adder_2_sum1, een_4bit_ripple_carry_adder_2_sum2,
       een_4bit_ripple_carry_adder_2_sum3, een_4bit_ripple_carry_adder_2_sum4,
       een_4x1_vermenigvuldiger_1_out1, een_4x1_vermenigvuldiger_1_out2, een_4x1_vermenigvuldiger_1_out3,
       een_4x1_vermenigvuldiger_2_out0, een_4x1_vermenigvuldiger_2_out1, een_4x1_vermenigvuldiger_2_out2,
       een_4x1_vermenigvuldiger_2_out3, een_4x1_vermenigvuldiger_3_out0, een_4x1_vermenigvuldiger_3_out1,
       een_4x1_vermenigvuldiger_3_out2, een_4x1_vermenigvuldiger_3_out3, een_4x1_vermenigvuldiger_4_out0,
       een_4x1_vermenigvuldiger_4_out1, een_4x1_vermenigvuldiger_4_out2, een_4x1_vermenigvuldiger_4_out3;

  Een_4X1_vermenigvuldiger een_4x1_vermenigvuldiger_1 (
    .X0(X0), .Y0(Y0), .Y1(Y1), .Y2(Y2), .Y3(Y3), .OUT3(een_4x1_vermenigvuldiger_1_out3),
    .OUT2(een_4x1_vermenigvuldiger_1_out2), .OUT1(een_4x1_vermenigvuldiger_1_out1), .OUT0(Z0));
  Een_4X1_vermenigvuldiger een_4x1_vermenigvuldiger_2 (
    .X0(X1), .Y0(Y0), .Y1(Y1), .Y2(Y2), .Y3(Y3), .OUT3(een_4x1_vermenigvuldiger_2_out3),
    .OUT2(een_4x1_vermenigvuldiger_2_out2), .OUT1(een_4x1_vermenigvuldiger_2_out1),
    .OUT0(een_4x1_vermenigvuldiger_2_out0));
  Een_4X1_vermenigvuldiger een_4x1_vermenigvuldiger_3 (
    .X0(X2), .Y0(Y0), .Y1(Y1), .Y2(Y2), .Y3(Y3), .OUT3(een_4x1_vermenigvuldiger_3_out3),
    .OUT2(een_4x1_vermenigvuldiger_3_out2), .OUT1(een_4x1_vermenigvuldiger_3_out1),
    .OUT0(een_4x1_vermenigvuldiger_3_out0));
  Een_4X1_vermenigvuldiger een_4x1_vermenigvuldiger_4 (
    .X0(X3), .Y0(Y0), .Y1(Y1), .Y2(Y2), .Y3(Y3), .OUT3(een_4x1_vermenigvuldiger_4_out3),
    .OUT2(een_4x1_vermenigvuldiger_4_out2), .OUT1(een_4x1_vermenigvuldiger_4_out1),
    .OUT0(een_4x1_vermenigvuldiger_4_out0));
  Een_4bit_Ripple_Carry_Adder een_4bit_ripple_carry_adder_1 (
    .Y3(een_4x1_vermenigvuldiger_2_out3), .Y2(een_4x1_vermenigvuldiger_2_out2),
    .Y1(een_4x1_vermenigvuldiger_2_out1), .Y0(een_4x1_vermenigvuldiger_2_out0),
    .X2(een_4x1_vermenigvuldiger_1_out3), .X1(een_4x1_vermenigvuldiger_1_out2),
    .X0(een_4x1_vermenigvuldiger_1_out1), .Sum4(een_4bit_ripple_carry_adder_1_sum4),
    .Sum3(een_4bit_ripple_carry_adder_1_sum3), .Sum2(een_4bit_ripple_carry_adder_1_sum2),
    .Sum1(een_4bit_ripple_carry_adder_1_sum1), .Sum0(Z1));  // open: X3
  Een_4bit_Ripple_Carry_Adder een_4bit_ripple_carry_adder_2 (
    .Y3(een_4x1_vermenigvuldiger_3_out3), .Y2(een_4x1_vermenigvuldiger_3_out2),
    .Y1(een_4x1_vermenigvuldiger_3_out1), .Y0(een_4x1_vermenigvuldiger_3_out0),
    .X3(een_4bit_ripple_carry_adder_1_sum4), .X2(een_4bit_ripple_carry_adder_1_sum3),
    .X1(een_4bit_ripple_carry_adder_1_sum2), .X0(een_4bit_ripple_carry_adder_1_sum1),
    .Sum4(een_4bit_ripple_carry_adder_2_sum4), .Sum3(een_4bit_ripple_carry_adder_2_sum3),
    .Sum2(een_4bit_ripple_carry_adder_2_sum2), .Sum1(een_4bit_ripple_carry_adder_2_sum1), .Sum0(Z2));
  Een_4bit_Ripple_Carry_Adder een_4bit_ripple_carry_adder_3 (
    .Y3(een_4x1_vermenigvuldiger_4_out3), .Y2(een_4x1_vermenigvuldiger_4_out2),
    .Y1(een_4x1_vermenigvuldiger_4_out1), .Y0(een_4x1_vermenigvuldiger_4_out0),
    .X3(een_4bit_ripple_carry_adder_2_sum4), .X2(een_4bit_ripple_carry_adder_2_sum3),
    .X1(een_4bit_ripple_carry_adder_2_sum2), .X0(een_4bit_ripple_carry_adder_2_sum1), .Sum4(Z7), .Sum3(Z6),
    .Sum2(Z5), .Sum1(Z4), .Sum0(Z3));

  // Notes on the sheet:
  //   factor (4 bits)
  //   See the problem for details on this hint:   Build a 4x1-bit multiplier first!
  //   tweede factor (4 bits)
  //   4-bit-VERMENIGVULDIGINGSschakeling
  //   meest significante (hoogste) uitvoerbit
  //   minst significante (laagste) uitvoerbit
  //   product (8 bits)
endmodule

module Een_3bij2_deler (
  input  Y2,
  input  Y1,
  input  Y0,
  input  X1,
  input  X0,
  output Z0,
  output Z1,
  output Z2,
  output Error
);

  wire and_2_out, and_3_out, and_4_out, and_5_out, and_6_out, and_7_out, and_9_out, not_1_out, not_2_out,
       not_3_out, not_4_out, not_5_out, not_6_out, not_7_out;

  not not_1 (not_1_out, X1);
  not not_2 (not_2_out, X1);
  not not_3 (not_3_out, X1);
  not not_4 (not_4_out, X1);
  not not_5 (not_5_out, X0);
  not not_6 (not_6_out, X0);
  not not_7 (not_7_out, X0);
  and and_1 (Error, not_5_out, not_1_out);
  and and_2 (and_2_out, Y1, Y0, X1, X0);
  and and_3 (and_3_out, X0, not_2_out, Y0);
  and and_4 (and_4_out, X1, X0, Y1, Y2);
  and and_5 (and_5_out, X0, not_3_out, Y1);
  and and_6 (and_6_out, X1, not_6_out, Y1);
  and and_7 (and_7_out, X1, X0, Y2);
  and and_8 (Z2, X0, not_4_out, Y2);
  and and_9 (and_9_out, X1, not_7_out, Y2);
  or or_1 (Z0, and_2_out, and_3_out, and_7_out, and_6_out);
  or or_2 (Z1, and_4_out, and_5_out, and_9_out);

  // Notes on the sheet:
  //   Teller (3 bits: Y2 Y1 Y0)
  //   Noemer (2 bits: X1 X0)
  //   Quotiënt (4 bits: Z2 Z1 Z0 en Error)
  //   3-bij-2-bit-DELINGSschakeling
endmodule

module Een_2bit_decoder (
  input  Input1,
  input  Input0,
  output Output3,
  output Output2,
  output Output1,
  output Output0
);

  wire not_1_out, not_2_out;

  not not_1 (not_1_out, Input1);
  not not_2 (not_2_out, Input0);
  and and_1 (Output3, Input0, Input1);
  and and_2 (Output2, not_2_out, Input1);
  and and_3 (Output1, Input0, not_1_out);
  and and_4 (Output0, not_2_out, not_1_out);

  // Notes on the sheet:
  //   2-bit-DECODERschakeling (bonusopgave)
endmodule

module Een_4X1_vermenigvuldiger (
  input  X0,
  input  Y0,
  input  Y1,
  input  Y2,
  input  Y3,
  output OUT3,
  output OUT2,
  output OUT1,
  output OUT0
);

  and and_1 (OUT3, X0, Y3);
  and and_2 (OUT2, X0, Y2);
  and and_3 (OUT1, X0, Y1);
  and and_4 (OUT0, X0, Y0);
endmodule

module SR_Latch (
  input  S,
  input  R,
  output Q
);

  wire nor_1_out;

  nor nor_1 (nor_1_out, S, Q);
  nor nor_2 (Q, nor_1_out, R);
endmodule

module Flip_Flop (
  input  D,
  input  Strobe,
  output q
);

  wire and_1_out, and_2_out, not_1_out;

  not not_1 (not_1_out, D);
  and and_1 (and_1_out, D, D, Strobe);
  and and_2 (and_2_out, not_1_out, Strobe);
  SR_Latch sr_latch_1 (.S(and_1_out), .R(and_2_out), .Q(q));
endmodule

module Een_12_nGb_geheugen (
  input  a1,
  input  a0,
  input  Data2,
  input  Data1,
  input  Data0,
  input  Read,
  input  Write,
  output Out2,
  output Out1,
  output Out0
);

  wire and_1_out, and_2_out, and_3_out, and_4_out, and_5_out, and_6_out, and_7_out, and_8_out, and_9_out,
       and_10_out, een_2bit_decoder_1_output0, een_2bit_decoder_1_output1, een_2bit_decoder_1_output2,
       een_2bit_decoder_1_output3, een_data_pass_1_out0, een_data_pass_1_out1, een_data_pass_1_out2,
       een_data_pass_2_out0, een_data_pass_2_out1, een_data_pass_2_out2, een_data_pass_3_out0,
       een_data_pass_3_out1, een_data_pass_3_out2, een_data_pass_4_out0, een_data_pass_4_out1,
       een_data_pass_4_out2, Locatie0_out0, Locatie0_out1, Locatie0_out2, Locatie1_out0, Locatie1_out1,
       Locatie1_out2, Locatie2_out0, Locatie2_out1, Locatie2_out2, Locatie3_out0, Locatie3_out1,
       Locatie3_out2, xor_1_out;

  and and_1 (and_1_out, and_6_out, een_2bit_decoder_1_output0);
  and and_2 (and_2_out, een_2bit_decoder_1_output1, and_6_out);
  Een_2bit_decoder een_2bit_decoder_1 (
    .Input1(a1), .Input0(a0), .Output3(een_2bit_decoder_1_output3), .Output2(een_2bit_decoder_1_output2),
    .Output1(een_2bit_decoder_1_output1), .Output0(een_2bit_decoder_1_output0));
  and and_3 (and_3_out, een_2bit_decoder_1_output2, and_6_out);
  and and_4 (and_4_out, and_6_out, een_2bit_decoder_1_output3);
  and and_5 (and_5_out, een_2bit_decoder_1_output0, and_7_out);
  Een_3bit_geheugen Locatie0 (
    .Strobe(and_5_out), .Data2(Data2), .Data1(Data1), .Data0(Data0), .Out0(Locatie0_out0),
    .Out1(Locatie0_out1), .Out2(Locatie0_out2));
  xor xor_1 (xor_1_out, Read, Write);
  and and_6 (and_6_out, Read, xor_1_out);
  and and_7 (and_7_out, xor_1_out, Write);
  and and_8 (and_8_out, een_2bit_decoder_1_output1, and_7_out);
  Een_3bit_geheugen Locatie1 (
    .Strobe(and_8_out), .Data2(Data2), .Data1(Data1), .Data0(Data0), .Out0(Locatie1_out0),
    .Out1(Locatie1_out1), .Out2(Locatie1_out2));
  and and_9 (and_9_out, een_2bit_decoder_1_output2, and_7_out);
  Een_3bit_geheugen Locatie2 (
    .Strobe(and_9_out), .Data2(Data2), .Data1(Data1), .Data0(Data0), .Out0(Locatie2_out0),
    .Out1(Locatie2_out1), .Out2(Locatie2_out2));
  and and_10 (and_10_out, een_2bit_decoder_1_output3, and_7_out);
  Een_3bit_geheugen Locatie3 (
    .Strobe(and_10_out), .Data2(Data2), .Data1(Data1), .Data0(Data0), .Out0(Locatie3_out0),
    .Out1(Locatie3_out1), .Out2(Locatie3_out2));
  Een_Data_Pass een_data_pass_1 (
    .Data0(Locatie1_out0), .Data1(Locatie1_out1), .Data2(Locatie1_out2), .Pass(and_2_out),
    .Out2(een_data_pass_1_out2), .Out1(een_data_pass_1_out1), .Out0(een_data_pass_1_out0));
  Een_Data_Pass een_data_pass_2 (
    .Data0(Locatie0_out0), .Data1(Locatie0_out1), .Data2(Locatie0_out2), .Pass(and_1_out),
    .Out2(een_data_pass_2_out2), .Out1(een_data_pass_2_out1), .Out0(een_data_pass_2_out0));
  Een_Data_Pass een_data_pass_3 (
    .Data0(Locatie3_out0), .Data1(Locatie3_out1), .Data2(Locatie3_out2), .Pass(and_4_out),
    .Out2(een_data_pass_3_out2), .Out1(een_data_pass_3_out1), .Out0(een_data_pass_3_out0));
  Een_Data_Pass een_data_pass_4 (
    .Data0(Locatie2_out0), .Data1(Locatie2_out1), .Data2(Locatie2_out2), .Pass(and_3_out),
    .Out2(een_data_pass_4_out2), .Out1(een_data_pass_4_out1), .Out0(een_data_pass_4_out0));
  or or_1 (Out2, een_data_pass_3_out2, een_data_pass_4_out2, een_data_pass_1_out2, een_data_pass_2_out2);
  or or_2 (Out1, een_data_pass_3_out1, een_data_pass_4_out1, een_data_pass_1_out1, een_data_pass_2_out1);
  or or_3 (Out0, een_data_pass_3_out0, een_data_pass_4_out0, een_data_pass_1_out0, een_data_pass_2_out0);
endmodule

module Een_3bit_geheugen (
  input  Strobe,
  input  Data2,
  input  Data1,
  input  Data0,
  output Out0,
  output Out1,
  output Out2
);

  Flip_Flop flip_flop_1 (.D(Data0), .Strobe(Strobe), .q(Out0));
  Flip_Flop flip_flop_2 (.D(Data1), .Strobe(Strobe), .q(Out1));
  Flip_Flop flip_flop_3 (.D(Data2), .Strobe(Strobe), .q(Out2));
endmodule

module Een_Data_Pass (
  input  Data0,
  input  Data1,
  input  Data2,
  input  Pass,
  output Out2,
  output Out1,
  output Out0
);

  and and_1 (Out0, Pass, Data0);
  and and_2 (Out1, Pass, Data1);
  and and_3 (Out2, Pass, Data2);
endmodule
